// Logisim project main.circ as structural Verilog: 1 circuit, main circuit main
module main (
);

  wire A_READ, A_WRITE, adder_1_cout, ALU_READ, ALU_WRITE, and_2_out, and_4_out, and_5_out, and_6_out,
       B_READ, B_WRITE, button_1_out, CARRY, CLK, IN_READ, IR_WRITE, MAR_READ, MAR_WRITE, nor_1_out,
       not_1_out, not_2_out, not_3_out, not_4_out, or_2_out, or_3_out, OUT_WRITE, PC_COUNT, PC_READ_A,
       PC_WRITE, RAM_ADDR_SEL, RAM_READ, RAM_WRITE, READ_EN, RESET, subtractor_1_bout, ZERO, ZERO_READ;
  wire [1:0] comparator_1_eq;
  wire [2:0] controlled_buffer_4_out;
  wire [3:0] binairy_to_bcd_converter_1_p3, binairy_to_bcd_converter_1_p4, binairy_to_bcd_converter_1_p5;
  wire [4:0] controlled_buffer_4_out_2;
  wire [7:0] A_q, adder_1_out, ALU_q, B_q, IR_q, MAR_q, multiplexer_1_out, multiplexer_2_out, nand_1_out,
       PC_q, ram_1_data, register_1_q, shifter_1_out, subtractor_1_out;

  Clock clock_1 (.out(CLK));
  Button button_1 (.out(button_1_out));
  Register MAR (.D(ram_1_data), .en(MAR_WRITE), .clk(CLK), .Q(MAR_q));  // open: clr
  not not_1 (not_1_out, CLK);
  D_Flip_Flop d_ff_1 (.D(READ_EN), .clk(CLK), .Q(IR_WRITE), .Qn(READ_EN), .reset(RESET));  // open: preset
  Counter PC (.load(PC_WRITE), .D(ram_1_data), .count(PC_COUNT), .Q(PC_q), .clk(CLK), .clr(RESET));  // open: carry, up
  and and_1 (RESET, not_1_out, button_1_out);
  Multiplexer #(.enable("false"), .width(8)) multiplexer_1 (
    .in0(PC_q), .in1(MAR_q), .out(multiplexer_1_out), .sel(RAM_ADDR_SEL));
  and and_2 (and_2_out, READ_EN, PC_READ_A);
  RAM #(.databus("bidir"), .readbehav("war"), .trigger("falling"), .\type ("nonvolatile")) ram_1 (
    .addr(multiplexer_1_out), .we(RAM_WRITE), .oe(RAM_READ), .clk(CLK), .data(ram_1_data));
  or or_1 (PC_COUNT, IR_WRITE, and_2_out);
  not not_2 (not_2_out, or_3_out);
  or or_2 (or_2_out, RAM_WRITE, MAR_READ);
  or or_3 (or_3_out, PC_READ_A, IR_WRITE);
  and and_3 (RAM_ADDR_SEL, not_2_out, or_2_out);
  or or_4 (RAM_READ, or_3_out, MAR_READ);
  assign ram_1_data = ZERO_READ ? {8{1'b0}} : 8'bz;  // Controlled_Buffer controlled_buffer_1
  // Probe on ram_1_data
  Register IR (.D(ram_1_data), .en(IR_WRITE), .clk(CLK), .Q(IR_q));  // open: clr
  Register register_1 (.D(ram_1_data), .en(OUT_WRITE), .clk(CLK), .Q(register_1_q));  // open: clr
  Register A (.D(ram_1_data), .en(A_WRITE), .clk(CLK), .Q(A_q));  // open: clr
  Register B (.D(ram_1_data), .en(B_WRITE), .clk(CLK), .Q(B_q));  // open: clr
  Register ALU (.D(ram_1_data), .en(ALU_WRITE), .clk(CLK), .Q(ALU_q));  // open: clr
  Hex_Digit_Display hex_digit_display_1 (.value(binairy_to_bcd_converter_1_p3));  // open: dp
  // Binairy_to_BCD_converter #(.binvalue(8)) binairy_to_bcd_converter_1: pin names not known; wires that end beside it: ram_1_data, register_1_q, binairy_to_bcd_converter_1_p3, binairy_to_bcd_converter_1_p4, binairy_to_bcd_converter_1_p5
  assign ram_1_data = A_READ ? A_q : 8'bz;  // Controlled_Buffer controlled_buffer_2
  assign ram_1_data = B_READ ? B_q : 8'bz;  // Controlled_Buffer controlled_buffer_3
  not not_3 (not_3_out, ZERO);
  not not_4 (not_4_out, CARRY);
  Hex_Digit_Display hex_digit_display_2 (.value(binairy_to_bcd_converter_1_p4));  // open: dp
  // Probe on IR_q[2:0]
  // Probe on IR_q[5:3]
  and and_4 (and_4_out, IR_q[6], not_3_out);
  and and_5 (and_5_out, IR_q[7], not_4_out);
  Hex_Digit_Display hex_digit_display_3 (.value(binairy_to_bcd_converter_1_p5));  // open: dp
  assign {controlled_buffer_4_out_2, controlled_buffer_4_out} = ALU_q[5] ? B_q : 8'bz;  // Controlled_Buffer controlled_buffer_4
  assign {controlled_buffer_4_out_2, controlled_buffer_4_out} = ALU_q[6] ? 8'h1 : 8'bz;  // Controlled_Buffer controlled_buffer_5
  Pull_Resistor pull_resistor_1 (.node({controlled_buffer_4_out_2, controlled_buffer_4_out}));
  nor nor_1 (nor_1_out, and_4_out, and_5_out);
  and and_6 (and_6_out, nor_1_out, READ_EN);
  assign ram_1_data = ALU_READ ? multiplexer_2_out : 8'bz;  // Controlled_Buffer controlled_buffer_6
  Adder adder_1 (
    .a(A_q), .b({controlled_buffer_4_out_2, controlled_buffer_4_out}), .out(adder_1_out), .cin(ALU_q[7]),
    .cout(adder_1_cout));
  Subtractor subtractor_1 (
    .a(A_q), .b({controlled_buffer_4_out_2, controlled_buffer_4_out}), .out(subtractor_1_out),
    .bin(ALU_q[7]), .bout(subtractor_1_bout));
  assign nand_1_out = ~(A_q & {controlled_buffer_4_out_2, controlled_buffer_4_out});  // NAND_Gate nand_1, 8 bits wide
  Shifter shifter_1 (.in(A_q), .\dist (controlled_buffer_4_out), .out(shifter_1_out));
  Decoder #(.select(3)) decoder_1 (
    .out0(ZERO_READ), .out1(PC_READ_A), .out2(MAR_READ), .out3(A_READ), .out4(B_READ), .out5(ALU_READ),
    .out7(IN_READ), .sel(IR_q[2:0]), .en(READ_EN));  // open: out6
  Decoder #(.select(3)) decoder_2 (
    .out0(RAM_WRITE), .out1(PC_WRITE), .out2(MAR_WRITE), .out3(A_WRITE), .out4(B_WRITE), .out5(ALU_WRITE),
    .out7(OUT_WRITE), .sel(IR_q[5:3]), .en(and_6_out));  // open: out6
  Multiplexer #(.enable("false"), .select(2), .width(8)) multiplexer_2 (
    .in0(adder_1_out), .in1(subtractor_1_out), .in2(nand_1_out), .in3(shifter_1_out),
    .out(multiplexer_2_out), .sel(ALU_q[1:0]));
  // Probe on multiplexer_2_out
  Multiplexer #(.enable("false"), .select(2)) multiplexer_3 (
    .in0(adder_1_cout), .in1(subtractor_1_bout), .out(comparator_1_eq[1]), .sel(ALU_q[1:0]));  // open: in2, in3
  Comparator comparator_1 (.a(multiplexer_2_out), .b({8{1'b0}}), .eq(comparator_1_eq[0]));  // open: gt, lt
  Register #(.trigger("falling"), .width(2)) register_2 (
    .D(comparator_1_eq), .en(ALU_WRITE), .clk(CLK), .Q({CARRY, ZERO}));  // open: clr

  // Other names for the same wires on the sheet: PC_READ_B = IR_WRITE; PC_SEL = IR_WRITE; WRITE_EN = READ_EN
endmodule
